# Fritzing sketch LunaStep Demo - Copy (saved by Fritzing 0.9.2b)
breadboards: 1

parts:
  Part1 = Arduino Uno (Rev3)
  S1 = Pushbutton [package="[THT]"]
  R1 = Resistor [tolerance=±5% resistance=220 package=THT]
  R2 = Resistor [tolerance=±5% resistance=220 package=THT]

nets:
  N1: Part1.D8, R1.Pin_0
  N2: Part1.GND, R2.Pin_0
  N3: Part1.5V, S1.Pin_1, S1.Pin_2
  N4: S1.Pin_3, S1.Pin_4, R1.Pin_1, R2.Pin_1

// code stored in the sketch: LunaStep Demo.ino
int val = 0;

void setup() {
  pinMode( 8, INPUT );

 Serial.begin( 9600 ); //Start serial on 9600 baud
}

void loop() {
  if( digitalRead( 8 ) == HIGH ) { // If mat/button is triggered, write to the serial monitor
    Serial.println( "Circut complete" );
    val++;
    Serial.println( val );
  }

  delay( 1000 ); // This is here to prevent from spamming the serial monitor
}
